# Fritzing sketch BlinkyButton (saved by Fritzing 0.9.2b)
breadboards: 1

parts:
  S1 = SWITCH-MOMENTARY-2 [package=tactile-pth]
  NEOPIXEL1 = Neopixel Strip -- White (60/m)
  MOTOR1 = Vibration Motor
  Part1 = Photon
  R1 = Resistor [tolerance=±10% resistance=10k package="0805 [SMD]"]
  R2 = Resistor [tolerance=±20% resistance=47k package="2010 [SMD]"]
  R3 = Resistor [tolerance=±5% resistance=33k package="2010 [SMD]"]
  U1 = LIPO-1000mAh [package=lipo-1000]

nets:
  GND: S1.1, NEOPIXEL1.GND, MOTOR1.NEG, Part1.GND, R3.Pin_1, U1.-
  +5V: NEOPIXEL1.+5V, Part1.VIN, R1.Pin_0
  N1: NEOPIXEL1.DI, Part1.D3
  N2: MOTOR1.POS, Part1.D5
  N3: Part1.A5, R2.Pin_1, R3.Pin_0
  N4: Part1.D4, R1.Pin_1
  N5: R2.Pin_0, U1.+

custom parts:
  Neopixel Strip -- White (60/m): Neopixel Strip, White, 60 pixels per meter.
  Vibration Motor: An eccentric vibration motor!
